// Digital circuit ula_32bits.dig as structural Verilog
module ula_32bits (
  input  [2:0] F,
  input  [31:0] A,
  input  [31:0] B,
  output neg,
  output overflow,
  output zero,
  output [31:0] R
);

  wire and_2_out, and_3_out, and_4_out, and_5_out, and_6_out, and_7_out, and_8_out, and_9_out, and_10_out,
       and_11_out, and_12_out, and_13_out, and_14_out, and_15_out, and_16_out, and_17_out, and_18_out,
       and_19_out, and_20_out, and_21_out, and_22_out, and_23_out, and_24_out, and_25_out, and_26_out,
       and_27_out, and_28_out, and_29_out, and_30_out, and_31_out, and_32_out, and_33_out, and_34_out,
       full_adder_1_soma, full_adder_1_vai, full_adder_2_soma, full_adder_2_vai, full_adder_3_soma,
       full_adder_3_vai, full_adder_4_soma, full_adder_4_vai, full_adder_5_soma, full_adder_5_vai,
       full_adder_6_soma, full_adder_6_vai, full_adder_7_soma, full_adder_7_vai, full_adder_8_soma,
       full_adder_8_vai, full_adder_9_soma, full_adder_9_vai, full_adder_10_soma, full_adder_10_vai,
       full_adder_11_soma, full_adder_11_vai, full_adder_12_soma, full_adder_12_vai, full_adder_13_soma,
       full_adder_13_vai, full_adder_14_soma, full_adder_14_vai, full_adder_15_soma, full_adder_15_vai,
       full_adder_16_soma, full_adder_16_vai, full_adder_17_soma, full_adder_17_vai, full_adder_18_soma,
       full_adder_18_vai, full_adder_19_soma, full_adder_19_vai, full_adder_20_soma, full_adder_20_vai,
       full_adder_21_soma, full_adder_21_vai, full_adder_22_soma, full_adder_22_vai, full_adder_23_soma,
       full_adder_23_vai, full_adder_24_soma, full_adder_24_vai, full_adder_25_soma, full_adder_25_vai,
       full_adder_26_soma, full_adder_26_vai, full_adder_27_soma, full_adder_27_vai, full_adder_28_soma,
       full_adder_28_vai, full_adder_29_soma, full_adder_29_vai, full_adder_30_soma, full_adder_30_vai,
       full_adder_31_soma, full_adder_31_vai, full_adder_32_soma, full_adder_32_vai, multiplexer_1_out,
       multiplexer_3_out, multiplexer_5_out, multiplexer_6_out, multiplexer_7_out, multiplexer_9_out,
       multiplexer_11_out, multiplexer_13_out, multiplexer_15_out, multiplexer_17_out, multiplexer_19_out,
       multiplexer_21_out, multiplexer_23_out, multiplexer_25_out, multiplexer_27_out, multiplexer_29_out,
       multiplexer_31_out, multiplexer_33_out, multiplexer_35_out, multiplexer_37_out, multiplexer_39_out,
       multiplexer_41_out, multiplexer_43_out, multiplexer_45_out, multiplexer_47_out, multiplexer_49_out,
       multiplexer_51_out, multiplexer_53_out, multiplexer_55_out, multiplexer_57_out, multiplexer_59_out,
       multiplexer_61_out, multiplexer_63_out, not_1_out, not_2_out, not_3_out, not_4_out, not_5_out,
       not_6_out, not_7_out, not_8_out, not_9_out, not_10_out, not_11_out, not_12_out, not_13_out,
       not_14_out, not_15_out, not_16_out, not_17_out, not_18_out, not_19_out, not_20_out, not_21_out,
       not_22_out, not_23_out, not_24_out, not_25_out, not_26_out, not_27_out, not_28_out, not_29_out,
       not_30_out, not_31_out, not_32_out, not_33_out, not_34_out, or_1_out, or_2_out, or_3_out, or_4_out,
       or_5_out, or_6_out, or_7_out, or_8_out, or_9_out, or_10_out, or_11_out, or_12_out, or_13_out,
       or_14_out, or_15_out, or_16_out, or_17_out, or_18_out, or_19_out, or_20_out, or_21_out, or_22_out,
       or_23_out, or_24_out, or_25_out, or_26_out, or_27_out, or_28_out, or_29_out, or_30_out, or_31_out,
       or_32_out, xor_2_out, xor_3_out, xor_4_out, xor_5_out, xor_6_out, xor_7_out, xor_8_out, xor_9_out,
       xor_10_out, xor_11_out, xor_12_out, xor_13_out, xor_14_out, xor_15_out, xor_16_out, xor_17_out,
       xor_18_out, xor_19_out, xor_20_out, xor_21_out, xor_22_out, xor_23_out, xor_24_out, xor_25_out,
       xor_26_out, xor_27_out, xor_28_out, xor_29_out, xor_30_out, xor_31_out, xor_32_out, xor_33_out;

  and and_1 (zero, ~neg, ~R[30], ~multiplexer_6_out, ~R[28], ~R[27], ~R[26], ~R[25], ~R[24], ~R[23], ~R[22], ~R[21], ~R[20], ~R[19], ~R[18], ~R[17], ~R[16], ~R[15], ~R[14], ~R[13], ~R[12], ~R[11], ~R[10], ~R[9], ~R[8], ~R[7], ~R[6], ~R[5], ~R[4], ~R[3], ~R[2], ~R[1], ~R[0]);  // And
  xor xor_1 (overflow, full_adder_2_vai, full_adder_1_vai);
  not not_1 (not_1_out, B[31]);
  and and_2 (and_2_out, B[31], A[31]);
  Multiplexer multiplexer_1 (.sel(and_34_out), .in_0(B[31]), .in_1(not_1_out), .out(multiplexer_1_out));
  full_adder full_adder_1 (
    .a(A[31]), .b(multiplexer_1_out), .vem(full_adder_2_vai), .vai(full_adder_1_vai), .soma(full_adder_1_soma));
  or or_1 (or_1_out, B[31], A[31]);
  xor xor_2 (xor_2_out, B[31], A[31]);
  Multiplexer #(.Selector_Bits(3)) multiplexer_2 (
    .sel(F), .in_0(full_adder_1_soma), .in_1(full_adder_1_soma), .in_2(xor_2_out), .in_3(or_1_out),
    .in_4(and_2_out), .in_5(1'b0), .in_6(1'b0), .in_7(1'b0), .out(neg));
  not not_2 (not_2_out, B[30]);
  Multiplexer multiplexer_3 (.sel(and_34_out), .in_0(B[30]), .in_1(not_2_out), .out(multiplexer_3_out));
  and and_3 (and_3_out, B[30], A[30]);
  full_adder full_adder_2 (
    .a(A[30]), .b(multiplexer_3_out), .vem(full_adder_3_vai), .vai(full_adder_2_vai), .soma(full_adder_2_soma));
  or or_2 (or_2_out, B[30], A[30]);
  xor xor_3 (xor_3_out, B[30], A[30]);
  Multiplexer #(.Selector_Bits(3)) multiplexer_4 (
    .sel(F), .in_0(full_adder_2_soma), .in_1(full_adder_2_soma), .in_2(xor_3_out), .in_3(or_2_out),
    .in_4(and_3_out), .in_5(1'b0), .in_6(1'b0), .in_7(1'b0), .out(R[30]));
  not not_3 (not_3_out, B[29]);
  and and_4 (and_4_out, B[29], A[29]);
  Multiplexer multiplexer_5 (.sel(and_34_out), .in_0(B[29]), .in_1(not_3_out), .out(multiplexer_5_out));
  full_adder full_adder_3 (
    .a(A[29]), .b(multiplexer_5_out), .vem(full_adder_4_vai), .vai(full_adder_3_vai), .soma(full_adder_3_soma));
  or or_3 (or_3_out, B[29], A[29]);
  xor xor_4 (xor_4_out, B[29], A[29]);
  Multiplexer #(.Selector_Bits(3)) multiplexer_6 (
    .sel(F), .in_0(full_adder_3_soma), .in_1(full_adder_3_soma), .in_2(xor_4_out), .in_3(or_3_out),
    .in_4(and_4_out), .in_5(1'b0), .in_6(1'b0), .in_7(1'b0), .out(multiplexer_6_out));
  not not_4 (not_4_out, B[28]);
  Multiplexer multiplexer_7 (.sel(and_34_out), .in_0(B[28]), .in_1(not_4_out), .out(multiplexer_7_out));
  and and_5 (and_5_out, B[28], A[28]);
  full_adder full_adder_4 (
    .a(A[28]), .b(multiplexer_7_out), .vem(full_adder_5_vai), .vai(full_adder_4_vai), .soma(full_adder_4_soma));
  or or_4 (or_4_out, B[28], A[28]);
  xor xor_5 (xor_5_out, B[28], A[28]);
  Multiplexer #(.Selector_Bits(3)) multiplexer_8 (
    .sel(F), .in_0(full_adder_4_soma), .in_1(full_adder_4_soma), .in_2(xor_5_out), .in_3(or_4_out),
    .in_4(and_5_out), .in_5(1'b0), .in_6(1'b0), .in_7(1'b0), .out(R[28]));
  not not_5 (not_5_out, B[27]);
  and and_6 (and_6_out, B[27], A[27]);
  Multiplexer multiplexer_9 (.sel(and_34_out), .in_0(B[27]), .in_1(not_5_out), .out(multiplexer_9_out));
  full_adder full_adder_5 (
    .a(A[27]), .b(multiplexer_9_out), .vem(full_adder_6_vai), .vai(full_adder_5_vai), .soma(full_adder_5_soma));
  or or_5 (or_5_out, B[27], A[27]);
  xor xor_6 (xor_6_out, B[27], A[27]);
  Multiplexer #(.Selector_Bits(3)) multiplexer_10 (
    .sel(F), .in_0(full_adder_5_soma), .in_1(full_adder_5_soma), .in_2(xor_6_out), .in_3(or_5_out),
    .in_4(and_6_out), .in_5(1'b0), .in_6(1'b0), .in_7(1'b0), .out(R[27]));
  not not_6 (not_6_out, B[26]);
  Multiplexer multiplexer_11 (.sel(and_34_out), .in_0(B[26]), .in_1(not_6_out), .out(multiplexer_11_out));
  and and_7 (and_7_out, B[26], A[26]);
  full_adder full_adder_6 (
    .a(A[26]), .b(multiplexer_11_out), .vem(full_adder_7_vai), .vai(full_adder_6_vai),
    .soma(full_adder_6_soma));
  or or_6 (or_6_out, B[26], A[26]);
  xor xor_7 (xor_7_out, B[26], A[26]);
  Multiplexer #(.Selector_Bits(3)) multiplexer_12 (
    .sel(F), .in_0(full_adder_6_soma), .in_1(full_adder_6_soma), .in_2(xor_7_out), .in_3(or_6_out),
    .in_4(and_7_out), .in_5(1'b0), .in_6(1'b0), .in_7(1'b0), .out(R[26]));
  not not_7 (not_7_out, B[25]);
  and and_8 (and_8_out, B[25], A[25]);
  Multiplexer multiplexer_13 (.sel(and_34_out), .in_0(B[25]), .in_1(not_7_out), .out(multiplexer_13_out));
  full_adder full_adder_7 (
    .a(A[25]), .b(multiplexer_13_out), .vem(full_adder_8_vai), .vai(full_adder_7_vai),
    .soma(full_adder_7_soma));
  or or_7 (or_7_out, B[25], A[25]);
  xor xor_8 (xor_8_out, B[25], A[25]);
  Multiplexer #(.Selector_Bits(3)) multiplexer_14 (
    .sel(F), .in_0(full_adder_7_soma), .in_1(full_adder_7_soma), .in_2(xor_8_out), .in_3(or_7_out),
    .in_4(and_8_out), .in_5(1'b0), .in_6(1'b0), .in_7(1'b0), .out(R[25]));
  not not_8 (not_8_out, B[24]);
  Multiplexer multiplexer_15 (.sel(and_34_out), .in_0(B[24]), .in_1(not_8_out), .out(multiplexer_15_out));
  and and_9 (and_9_out, B[24], A[24]);
  full_adder full_adder_8 (
    .a(A[24]), .b(multiplexer_15_out), .vem(full_adder_9_vai), .vai(full_adder_8_vai),
    .soma(full_adder_8_soma));
  or or_8 (or_8_out, B[24], A[24]);
  xor xor_9 (xor_9_out, B[24], A[24]);
  Multiplexer #(.Selector_Bits(3)) multiplexer_16 (
    .sel(F), .in_0(full_adder_8_soma), .in_1(full_adder_8_soma), .in_2(xor_9_out), .in_3(or_8_out),
    .in_4(and_9_out), .in_5(1'b0), .in_6(1'b0), .in_7(1'b0), .out(R[24]));
  not not_9 (not_9_out, B[23]);
  and and_10 (and_10_out, B[23], A[23]);
  Multiplexer multiplexer_17 (.sel(and_34_out), .in_0(B[23]), .in_1(not_9_out), .out(multiplexer_17_out));
  full_adder full_adder_9 (
    .a(A[23]), .b(multiplexer_17_out), .vem(full_adder_10_vai), .vai(full_adder_9_vai),
    .soma(full_adder_9_soma));
  or or_9 (or_9_out, B[23], A[23]);
  xor xor_10 (xor_10_out, B[23], A[23]);
  Multiplexer #(.Selector_Bits(3)) multiplexer_18 (
    .sel(F), .in_0(full_adder_9_soma), .in_1(full_adder_9_soma), .in_2(xor_10_out), .in_3(or_9_out),
    .in_4(and_10_out), .in_5(1'b0), .in_6(1'b0), .in_7(1'b0), .out(R[23]));
  not not_10 (not_10_out, B[22]);
  Multiplexer multiplexer_19 (.sel(and_34_out), .in_0(B[22]), .in_1(not_10_out), .out(multiplexer_19_out));
  and and_11 (and_11_out, B[22], A[22]);
  full_adder full_adder_10 (
    .a(A[22]), .b(multiplexer_19_out), .vem(full_adder_11_vai), .vai(full_adder_10_vai),
    .soma(full_adder_10_soma));
  or or_10 (or_10_out, B[22], A[22]);
  xor xor_11 (xor_11_out, B[22], A[22]);
  Multiplexer #(.Selector_Bits(3)) multiplexer_20 (
    .sel(F), .in_0(full_adder_10_soma), .in_1(full_adder_10_soma), .in_2(xor_11_out), .in_3(or_10_out),
    .in_4(and_11_out), .in_5(1'b0), .in_6(1'b0), .in_7(1'b0), .out(R[22]));
  not not_11 (not_11_out, B[21]);
  and and_12 (and_12_out, B[21], A[21]);
  Multiplexer multiplexer_21 (.sel(and_34_out), .in_0(B[21]), .in_1(not_11_out), .out(multiplexer_21_out));
  full_adder full_adder_11 (
    .a(A[21]), .b(multiplexer_21_out), .vem(full_adder_12_vai), .vai(full_adder_11_vai),
    .soma(full_adder_11_soma));
  or or_11 (or_11_out, B[21], A[21]);
  xor xor_12 (xor_12_out, B[21], A[21]);
  Multiplexer #(.Selector_Bits(3)) multiplexer_22 (
    .sel(F), .in_0(full_adder_11_soma), .in_1(full_adder_11_soma), .in_2(xor_12_out), .in_3(or_11_out),
    .in_4(and_12_out), .in_5(1'b0), .in_6(1'b0), .in_7(1'b0), .out(R[21]));
  not not_12 (not_12_out, B[20]);
  Multiplexer multiplexer_23 (.sel(and_34_out), .in_0(B[20]), .in_1(not_12_out), .out(multiplexer_23_out));
  and and_13 (and_13_out, B[20], A[20]);
  full_adder full_adder_12 (
    .a(A[20]), .b(multiplexer_23_out), .vem(full_adder_13_vai), .vai(full_adder_12_vai),
    .soma(full_adder_12_soma));
  or or_12 (or_12_out, B[20], A[20]);
  xor xor_13 (xor_13_out, B[20], A[20]);
  Multiplexer #(.Selector_Bits(3)) multiplexer_24 (
    .sel(F), .in_0(full_adder_12_soma), .in_1(full_adder_12_soma), .in_2(xor_13_out), .in_3(or_12_out),
    .in_4(and_13_out), .in_5(1'b0), .in_6(1'b0), .in_7(1'b0), .out(R[20]));
  not not_13 (not_13_out, B[19]);
  and and_14 (and_14_out, B[19], A[19]);
  Multiplexer multiplexer_25 (.sel(and_34_out), .in_0(B[19]), .in_1(not_13_out), .out(multiplexer_25_out));
  full_adder full_adder_13 (
    .a(A[19]), .b(multiplexer_25_out), .vem(full_adder_14_vai), .vai(full_adder_13_vai),
    .soma(full_adder_13_soma));
  or or_13 (or_13_out, B[19], A[19]);
  xor xor_14 (xor_14_out, B[19], A[19]);
  Multiplexer #(.Selector_Bits(3)) multiplexer_26 (
    .sel(F), .in_0(full_adder_13_soma), .in_1(full_adder_13_soma), .in_2(xor_14_out), .in_3(or_13_out),
    .in_4(and_14_out), .in_5(1'b0), .in_6(1'b0), .in_7(1'b0), .out(R[19]));
  not not_14 (not_14_out, B[18]);
  Multiplexer multiplexer_27 (.sel(and_34_out), .in_0(B[18]), .in_1(not_14_out), .out(multiplexer_27_out));
  and and_15 (and_15_out, B[18], A[18]);
  full_adder full_adder_14 (
    .a(A[18]), .b(multiplexer_27_out), .vem(full_adder_15_vai), .vai(full_adder_14_vai),
    .soma(full_adder_14_soma));
  or or_14 (or_14_out, B[18], A[18]);
  xor xor_15 (xor_15_out, B[18], A[18]);
  Multiplexer #(.Selector_Bits(3)) multiplexer_28 (
    .sel(F), .in_0(full_adder_14_soma), .in_1(full_adder_14_soma), .in_2(xor_15_out), .in_3(or_14_out),
    .in_4(and_15_out), .in_5(1'b0), .in_6(1'b0), .in_7(1'b0), .out(R[18]));
  not not_15 (not_15_out, B[17]);
  and and_16 (and_16_out, B[17], A[17]);
  Multiplexer multiplexer_29 (.sel(and_34_out), .in_0(B[17]), .in_1(not_15_out), .out(multiplexer_29_out));
  full_adder full_adder_15 (
    .a(A[17]), .b(multiplexer_29_out), .vem(full_adder_16_vai), .vai(full_adder_15_vai),
    .soma(full_adder_15_soma));
  or or_15 (or_15_out, B[17], A[17]);
  xor xor_16 (xor_16_out, B[17], A[17]);
  Multiplexer #(.Selector_Bits(3)) multiplexer_30 (
    .sel(F), .in_0(full_adder_15_soma), .in_1(full_adder_15_soma), .in_2(xor_16_out), .in_3(or_15_out),
    .in_4(and_16_out), .in_5(1'b0), .in_6(1'b0), .in_7(1'b0), .out(R[17]));
  not not_16 (not_16_out, B[16]);
  Multiplexer multiplexer_31 (.sel(and_34_out), .in_0(B[16]), .in_1(not_16_out), .out(multiplexer_31_out));
  and and_17 (and_17_out, B[16], A[16]);
  full_adder full_adder_16 (
    .a(A[16]), .b(multiplexer_31_out), .vem(full_adder_17_vai), .vai(full_adder_16_vai),
    .soma(full_adder_16_soma));
  or or_16 (or_16_out, B[16], A[16]);
  xor xor_17 (xor_17_out, B[16], A[16]);
  Multiplexer #(.Selector_Bits(3)) multiplexer_32 (
    .sel(F), .in_0(full_adder_16_soma), .in_1(full_adder_16_soma), .in_2(xor_17_out), .in_3(or_16_out),
    .in_4(and_17_out), .in_5(1'b0), .in_6(1'b0), .in_7(1'b0), .out(R[16]));
  not not_17 (not_17_out, B[15]);
  and and_18 (and_18_out, B[15], A[15]);
  Multiplexer multiplexer_33 (.sel(and_34_out), .in_0(B[15]), .in_1(not_17_out), .out(multiplexer_33_out));
  full_adder full_adder_17 (
    .a(A[15]), .b(multiplexer_33_out), .vem(full_adder_18_vai), .vai(full_adder_17_vai),
    .soma(full_adder_17_soma));
  or or_17 (or_17_out, B[15], A[15]);
  xor xor_18 (xor_18_out, B[15], A[15]);
  Multiplexer #(.Selector_Bits(3)) multiplexer_34 (
    .sel(F), .in_0(full_adder_17_soma), .in_1(full_adder_17_soma), .in_2(xor_18_out), .in_3(or_17_out),
    .in_4(and_18_out), .in_5(1'b0), .in_6(1'b0), .in_7(1'b0), .out(R[15]));
  not not_18 (not_18_out, B[14]);
  Multiplexer multiplexer_35 (.sel(and_34_out), .in_0(B[14]), .in_1(not_18_out), .out(multiplexer_35_out));
  and and_19 (and_19_out, B[14], A[14]);
  full_adder full_adder_18 (
    .a(A[14]), .b(multiplexer_35_out), .vem(full_adder_19_vai), .vai(full_adder_18_vai),
    .soma(full_adder_18_soma));
  or or_18 (or_18_out, B[14], A[14]);
  xor xor_19 (xor_19_out, B[14], A[14]);
  Multiplexer #(.Selector_Bits(3)) multiplexer_36 (
    .sel(F), .in_0(full_adder_18_soma), .in_1(full_adder_18_soma), .in_2(xor_19_out), .in_3(or_18_out),
    .in_4(and_19_out), .in_5(1'b0), .in_6(1'b0), .in_7(1'b0), .out(R[14]));
  not not_19 (not_19_out, B[13]);
  and and_20 (and_20_out, B[13], A[13]);
  Multiplexer multiplexer_37 (.sel(and_34_out), .in_0(B[13]), .in_1(not_19_out), .out(multiplexer_37_out));
  full_adder full_adder_19 (
    .a(A[13]), .b(multiplexer_37_out), .vem(full_adder_20_vai), .vai(full_adder_19_vai),
    .soma(full_adder_19_soma));
  or or_19 (or_19_out, B[13], A[13]);
  xor xor_20 (xor_20_out, B[13], A[13]);
  Multiplexer #(.Selector_Bits(3)) multiplexer_38 (
    .sel(F), .in_0(full_adder_19_soma), .in_1(full_adder_19_soma), .in_2(xor_20_out), .in_3(or_19_out),
    .in_4(and_20_out), .in_5(1'b0), .in_6(1'b0), .in_7(1'b0), .out(R[13]));
  not not_20 (not_20_out, B[12]);
  Multiplexer multiplexer_39 (.sel(and_34_out), .in_0(B[12]), .in_1(not_20_out), .out(multiplexer_39_out));
  and and_21 (and_21_out, B[12], A[12]);
  full_adder full_adder_20 (
    .a(A[12]), .b(multiplexer_39_out), .vem(full_adder_21_vai), .vai(full_adder_20_vai),
    .soma(full_adder_20_soma));
  or or_20 (or_20_out, B[12], A[12]);
  xor xor_21 (xor_21_out, B[12], A[12]);
  Multiplexer #(.Selector_Bits(3)) multiplexer_40 (
    .sel(F), .in_0(full_adder_20_soma), .in_1(full_adder_20_soma), .in_2(xor_21_out), .in_3(or_20_out),
    .in_4(and_21_out), .in_5(1'b0), .in_6(1'b0), .in_7(1'b0), .out(R[12]));
  not not_21 (not_21_out, B[11]);
  and and_22 (and_22_out, B[11], A[11]);
  Multiplexer multiplexer_41 (.sel(and_34_out), .in_0(B[11]), .in_1(not_21_out), .out(multiplexer_41_out));
  full_adder full_adder_21 (
    .a(A[11]), .b(multiplexer_41_out), .vem(full_adder_22_vai), .vai(full_adder_21_vai),
    .soma(full_adder_21_soma));
  or or_21 (or_21_out, B[11], A[11]);
  xor xor_22 (xor_22_out, B[11], A[11]);
  Multiplexer #(.Selector_Bits(3)) multiplexer_42 (
    .sel(F), .in_0(full_adder_21_soma), .in_1(full_adder_21_soma), .in_2(xor_22_out), .in_3(or_21_out),
    .in_4(and_22_out), .in_5(1'b0), .in_6(1'b0), .in_7(1'b0), .out(R[11]));
  not not_22 (not_22_out, B[10]);
  Multiplexer multiplexer_43 (.sel(and_34_out), .in_0(B[10]), .in_1(not_22_out), .out(multiplexer_43_out));
  and and_23 (and_23_out, B[10], A[10]);
  full_adder full_adder_22 (
    .a(A[10]), .b(multiplexer_43_out), .vem(full_adder_23_vai), .vai(full_adder_22_vai),
    .soma(full_adder_22_soma));
  or or_22 (or_22_out, B[10], A[10]);
  xor xor_23 (xor_23_out, B[10], A[10]);
  Multiplexer #(.Selector_Bits(3)) multiplexer_44 (
    .sel(F), .in_0(full_adder_22_soma), .in_1(full_adder_22_soma), .in_2(xor_23_out), .in_3(or_22_out),
    .in_4(and_23_out), .in_5(1'b0), .in_6(1'b0), .in_7(1'b0), .out(R[10]));
  not not_23 (not_23_out, B[9]);
  and and_24 (and_24_out, B[9], A[9]);
  Multiplexer multiplexer_45 (.sel(and_34_out), .in_0(B[9]), .in_1(not_23_out), .out(multiplexer_45_out));
  full_adder full_adder_23 (
    .a(A[9]), .b(multiplexer_45_out), .vem(full_adder_24_vai), .vai(full_adder_23_vai),
    .soma(full_adder_23_soma));
  or or_23 (or_23_out, B[9], A[9]);
  xor xor_24 (xor_24_out, B[9], A[9]);
  Multiplexer #(.Selector_Bits(3)) multiplexer_46 (
    .sel(F), .in_0(full_adder_23_soma), .in_1(full_adder_23_soma), .in_2(xor_24_out), .in_3(or_23_out),
    .in_4(and_24_out), .in_5(1'b0), .in_6(1'b0), .in_7(1'b0), .out(R[9]));
  not not_24 (not_24_out, B[8]);
  Multiplexer multiplexer_47 (.sel(and_34_out), .in_0(B[8]), .in_1(not_24_out), .out(multiplexer_47_out));
  and and_25 (and_25_out, B[8], A[8]);
  full_adder full_adder_24 (
    .a(A[8]), .b(multiplexer_47_out), .vem(full_adder_25_vai), .vai(full_adder_24_vai),
    .soma(full_adder_24_soma));
  or or_24 (or_24_out, B[8], A[8]);
  xor xor_25 (xor_25_out, B[8], A[8]);
  Multiplexer #(.Selector_Bits(3)) multiplexer_48 (
    .sel(F), .in_0(full_adder_24_soma), .in_1(full_adder_24_soma), .in_2(xor_25_out), .in_3(or_24_out),
    .in_4(and_25_out), .in_5(1'b0), .in_6(1'b0), .in_7(1'b0), .out(R[8]));
  not not_25 (not_25_out, B[7]);
  and and_26 (and_26_out, B[7], A[7]);
  Multiplexer multiplexer_49 (.sel(and_34_out), .in_0(B[7]), .in_1(not_25_out), .out(multiplexer_49_out));
  full_adder full_adder_25 (
    .a(A[7]), .b(multiplexer_49_out), .vem(full_adder_26_vai), .vai(full_adder_25_vai),
    .soma(full_adder_25_soma));
  or or_25 (or_25_out, B[7], A[7]);
  xor xor_26 (xor_26_out, B[7], A[7]);
  Multiplexer #(.Selector_Bits(3)) multiplexer_50 (
    .sel(F), .in_0(full_adder_25_soma), .in_1(full_adder_25_soma), .in_2(xor_26_out), .in_3(or_25_out),
    .in_4(and_26_out), .in_5(1'b0), .in_6(1'b0), .in_7(1'b0), .out(R[7]));
  not not_26 (not_26_out, B[6]);
  Multiplexer multiplexer_51 (.sel(and_34_out), .in_0(B[6]), .in_1(not_26_out), .out(multiplexer_51_out));
  and and_27 (and_27_out, B[6], A[6]);
  full_adder full_adder_26 (
    .a(A[6]), .b(multiplexer_51_out), .vem(full_adder_27_vai), .vai(full_adder_26_vai),
    .soma(full_adder_26_soma));
  or or_26 (or_26_out, B[6], A[6]);
  xor xor_27 (xor_27_out, B[6], A[6]);
  Multiplexer #(.Selector_Bits(3)) multiplexer_52 (
    .sel(F), .in_0(full_adder_26_soma), .in_1(full_adder_26_soma), .in_2(xor_27_out), .in_3(or_26_out),
    .in_4(and_27_out), .in_5(1'b0), .in_6(1'b0), .in_7(1'b0), .out(R[6]));
  not not_27 (not_27_out, B[5]);
  and and_28 (and_28_out, B[5], A[5]);
  Multiplexer multiplexer_53 (.sel(and_34_out), .in_0(B[5]), .in_1(not_27_out), .out(multiplexer_53_out));
  full_adder full_adder_27 (
    .a(A[5]), .b(multiplexer_53_out), .vem(full_adder_28_vai), .vai(full_adder_27_vai),
    .soma(full_adder_27_soma));
  or or_27 (or_27_out, B[5], A[5]);
  xor xor_28 (xor_28_out, B[5], A[5]);
  Multiplexer #(.Selector_Bits(3)) multiplexer_54 (
    .sel(F), .in_0(full_adder_27_soma), .in_1(full_adder_27_soma), .in_2(xor_28_out), .in_3(or_27_out),
    .in_4(and_28_out), .in_5(1'b0), .in_6(1'b0), .in_7(1'b0), .out(R[5]));
  not not_28 (not_28_out, B[4]);
  Multiplexer multiplexer_55 (.sel(and_34_out), .in_0(B[4]), .in_1(not_28_out), .out(multiplexer_55_out));
  and and_29 (and_29_out, B[4], A[4]);
  full_adder full_adder_28 (
    .a(A[4]), .b(multiplexer_55_out), .vem(full_adder_29_vai), .vai(full_adder_28_vai),
    .soma(full_adder_28_soma));
  or or_28 (or_28_out, B[4], A[4]);
  xor xor_29 (xor_29_out, B[4], A[4]);
  Multiplexer #(.Selector_Bits(3)) multiplexer_56 (
    .sel(F), .in_0(full_adder_28_soma), .in_1(full_adder_28_soma), .in_2(xor_29_out), .in_3(or_28_out),
    .in_4(and_29_out), .in_5(1'b0), .in_6(1'b0), .in_7(1'b0), .out(R[4]));
  not not_29 (not_29_out, B[3]);
  and and_30 (and_30_out, B[3], A[3]);
  Multiplexer multiplexer_57 (.sel(and_34_out), .in_0(B[3]), .in_1(not_29_out), .out(multiplexer_57_out));
  full_adder full_adder_29 (
    .a(A[3]), .b(multiplexer_57_out), .vem(full_adder_30_vai), .vai(full_adder_29_vai),
    .soma(full_adder_29_soma));
  or or_29 (or_29_out, B[3], A[3]);
  xor xor_30 (xor_30_out, B[3], A[3]);
  Multiplexer #(.Selector_Bits(3)) multiplexer_58 (
    .sel(F), .in_0(full_adder_29_soma), .in_1(full_adder_29_soma), .in_2(xor_30_out), .in_3(or_29_out),
    .in_4(and_30_out), .in_5(1'b0), .in_6(1'b0), .in_7(1'b0), .out(R[3]));
  not not_30 (not_30_out, B[2]);
  Multiplexer multiplexer_59 (.sel(and_34_out), .in_0(B[2]), .in_1(not_30_out), .out(multiplexer_59_out));
  and and_31 (and_31_out, B[2], A[2]);
  full_adder full_adder_30 (
    .a(A[2]), .b(multiplexer_59_out), .vem(full_adder_31_vai), .vai(full_adder_30_vai),
    .soma(full_adder_30_soma));
  or or_30 (or_30_out, B[2], A[2]);
  xor xor_31 (xor_31_out, B[2], A[2]);
  Multiplexer #(.Selector_Bits(3)) multiplexer_60 (
    .sel(F), .in_0(full_adder_30_soma), .in_1(full_adder_30_soma), .in_2(xor_31_out), .in_3(or_30_out),
    .in_4(and_31_out), .in_5(1'b0), .in_6(1'b0), .in_7(1'b0), .out(R[2]));
  not not_31 (not_31_out, B[1]);
  and and_32 (and_32_out, B[1], A[1]);
  Multiplexer multiplexer_61 (.sel(and_34_out), .in_0(B[1]), .in_1(not_31_out), .out(multiplexer_61_out));
  full_adder full_adder_31 (
    .a(A[1]), .b(multiplexer_61_out), .vem(full_adder_32_vai), .vai(full_adder_31_vai),
    .soma(full_adder_31_soma));
  or or_31 (or_31_out, B[1], A[1]);
  xor xor_32 (xor_32_out, B[1], A[1]);
  Multiplexer #(.Selector_Bits(3)) multiplexer_62 (
    .sel(F), .in_0(full_adder_31_soma), .in_1(full_adder_31_soma), .in_2(xor_32_out), .in_3(or_31_out),
    .in_4(and_32_out), .in_5(1'b0), .in_6(1'b0), .in_7(1'b0), .out(R[1]));
  not not_32 (not_32_out, B[0]);
  Multiplexer multiplexer_63 (.sel(and_34_out), .in_0(B[0]), .in_1(not_32_out), .out(multiplexer_63_out));
  and and_33 (and_33_out, B[0], A[0]);
  full_adder full_adder_32 (
    .a(A[0]), .b(multiplexer_63_out), .vem(and_34_out), .vai(full_adder_32_vai), .soma(full_adder_32_soma));
  or or_32 (or_32_out, B[0], A[0]);
  and and_34 (and_34_out, F[0], not_34_out, not_33_out);
  xor xor_33 (xor_33_out, B[0], A[0]);
  Multiplexer #(.Selector_Bits(3)) multiplexer_64 (
    .sel(F), .in_0(full_adder_32_soma), .in_1(full_adder_32_soma), .in_2(xor_33_out), .in_3(or_32_out),
    .in_4(and_33_out), .in_5(1'b0), .in_6(1'b0), .in_7(1'b0), .out(R[0]));
  not not_33 (not_33_out, F[2]);
  not not_34 (not_34_out, F[1]);

  assign {R[31], R[29]} = {neg, R[30]};
endmodule
